# Fritzing sketch modelo frizting e6 (saved by Fritzing 0.9.6b)
breadboards: 1

parts:
  Raspberry_Pi_1 = Raspberry Pi 3 [part_number=RPI-3-V1.2]
  R1 = Resistor [tolerance=±5% power=0.25 resistance=220 package=THT]
  R2 = Resistor [tolerance=±5% power=0.25 resistance=220 package=THT]
  LED1 = LED - 5mm [color="Red (633nm)" current=0.030 package="5 mm [THT]"]
  LED2 = LED - 5mm [color="Red (633nm)" current=0.030 package="5 mm [THT]"]
  S1 = Pushbutton [package="[THT]"]
  S2 = Pushbutton [package="[THT]"]

nets:
  N1: Raspberry_Pi_1.GIPO27, R1.Pin_1
  N2: Raspberry_Pi_1.GIPO18, S2.Pin_1, S2.Pin_2
  N3: Raspberry_Pi_1.GIPO15, R2.Pin_1
  N4: Raspberry_Pi_1.GIPO14, S1.Pin_1, S1.Pin_2
  N5: Raspberry_Pi_1.GND, LED1.cathode, LED2.cathode, S1.Pin_3, S1.Pin_4, S2.Pin_3, S2.Pin_4
  N6: R1.Pin_0, LED2.anode
  N7: R2.Pin_0, LED1.anode
